# Fritzing sketch Project_LibAcesso (saved by Fritzing 0.9.3b)
breadboards: 1

parts:
  Raspberry_Pi1 = Raspberry Pi 2
  LED1 = LED - 5mm [color="Red (633nm)" package="5 mm [THT]"]
  LED2 = LED - 5mm [color="Green (555nm)" package="5 mm [THT]"]
  R1 = Resistor [tolerance=±5% resistance=220 package=THT]
  R2 = Resistor [tolerance=±5% resistance=220 package=THT]
  LCD1 = LCD screen
  U1 = POT [package=pot_mammoth]
  J1 = Piezo Speaker
  Componente1 = RFID-RC522-v2

nets:
  3V3: Raspberry_Pi1.3v3, Componente1.3.3V
  GND: Raspberry_Pi1.GND, R1.Pin_1, R2.Pin_1, LCD1.VSS, LCD1.R/W, LCD1.LED-, U1.E, Componente1.GND
  N1: Raspberry_Pi1.GPIO17, LED1.anode
  N2: Raspberry_Pi1.GPIO27, LED2.anode
  N3: Raspberry_Pi1.GPIO22, J1.pin1
  N4: Raspberry_Pi1.GPIO10, Componente1.MOSI
  N5: Raspberry_Pi1.GPIO9, Componente1.MISO
  N6: Raspberry_Pi1.GPIO11, Componente1.SCK
  N7: Raspberry_Pi1.GPIO21, LCD1.DB7
  N8: Raspberry_Pi1.GPIO20, LCD1.DB6
  N9: Raspberry_Pi1.GPIO16, LCD1.DB5
  N10: Raspberry_Pi1.GPIO12, LCD1.DB4
  N11: Raspberry_Pi1.GPIO8, Componente1.SDA
  N12: Raspberry_Pi1.GPIO25, Componente1.RST
  N13: Raspberry_Pi1.GPIO23, LCD1.E
  N14: Raspberry_Pi1.GPIO18, LCD1.RS
  5V: Raspberry_Pi1.5V, LCD1.VDD, LCD1.LED+, U1.S, J1.pin2
  N15: LED1.cathode, R2.Pin_0
  N16: LED2.cathode, R1.Pin_0
  N17: LCD1.V0, U1.A

custom parts:
  RFID-RC522-v2: A simple China made RFID-RC522 Reader; do check the pin labels, as this is a MFRC522 based clone.
